// Logisim project ALU.circ as structural Verilog: 3 circuits, main circuit ALU
module ALU (
  input  [1:0] Control,
  input  [7:0] A,
  input  [7:0] B,
  output [7:0] Result,
  output Overflow
);

  wire [7:0] adder_1_out, and_1_out, multiplexer_1_out, negator_1_out, or_1_out;

  Negator negator_1 (.in(B), .out(negator_1_out));
  Multiplexer #(.width(8)) multiplexer_1 (.in0(B), .in1(negator_1_out), .out(multiplexer_1_out), .sel(Control[0]));
  assign and_1_out = A & B;  // AND_Gate and_1, 8 bits wide
  assign or_1_out = A | B;  // OR_Gate or_1, 8 bits wide
  Adder adder_1 (.a(A), .b(multiplexer_1_out), .out(adder_1_out), .cin(1'b0), .cout(Overflow));
  Multiplexer #(.select(2), .width(8)) multiplexer_2 (
    .in0(adder_1_out), .in1(adder_1_out), .in2(and_1_out), .in3(or_1_out), .out(Result), .sel(Control));
endmodule

module fulladder (
  input  Cin,
  input  A,
  input  B,
  output Result,
  output Cout
);

  wire and_1_out, and_2_out, xor_1_out;

  and and_1 (and_1_out, A, B);
  xor xor_1 (xor_1_out, A, B);
  or or_1 (Cout, and_1_out, and_2_out);
  and and_2 (and_2_out, Cin, xor_1_out);
  xor xor_2 (Result, Cin, xor_1_out);
endmodule

module mynegator (
  input  [3:0] A,
  output [3:0] two_complement_of_A
);

  wire or_1_out, or_2_out;

  or or_1 (or_1_out, A[2], or_2_out);
  xor xor_1 (two_complement_of_A[3], A[3], or_1_out);
  or or_2 (or_2_out, A[1], A[0]);
  xor xor_2 (two_complement_of_A[2], A[2], or_2_out);
  xor xor_3 (two_complement_of_A[1], A[1], A[0]);

  assign two_complement_of_A[0] = A[0];
endmodule
